# Fritzing sketch Platine (saved by Fritzing 0.9.4)
perfboards: 1

parts:
  Q8 = TRANSISTOR_NPN [package=to-92-ammo]
  Q5 = TRANSISTOR_NPN [package=to-92-ammo]
  Q9 = TRANSISTOR_NPN [package=to-92-ammo]
  Q6 = TRANSISTOR_NPN [package=to-92-ammo]
  Q7 = TRANSISTOR_NPN [package=to-92-ammo]

nets:
  N1: Q8.E, Q5.E, Q9.E, Q6.E, Q7.E

notes:
  GPIO ButtonLicht1
  GPIO Button1
  GPIO Button5
  GPIO ButtonLicht2
  12v
  GPIO ButtonLicht5
  GPIO ButtonLicht3
  GND
  3,3v
  GPIO Button2
  GPIO Button4
  GPIO ButtonLicht4
  GPIO Button3
